// Digital circuit CPU.dig as structural Verilog
module CPU (
  input  clk,
  input  clk_2,
  input  InspectMode,
  input  [4:0] InspectAddr
);

  wire AEq, AGreater, ALU_p26, ALU_p27, ALU_p28, ALUOut, and_1_out, and_2_out, and_3_out, and_4_out, AZero,
       clock_with_enable_1_clko, EnA, EnB, EnGnd, EnInst, Hi0, Hi1, Hi2, Hi3, HiA, HiB, HiC, HiD, HiDP, HiE,
       HiF, HiG, Hlt, LdA, LdB, LdFlags, LdInst, LdMAddr, LdOut, Lo0, Lo1, Lo2, Lo3, LoA, LoB, LoC, LoD,
       LoDP, LoE, LoF, LoG, MAddr_q5, MAddr_q6, MAddr_q7, MEn, MWr, not_2_out, not_3_out, not_4_out,
       or_1_out, or_2_out, or_3_out, PCClear, PCEnable, PCLd, PCOut, PrMode, Rdy, Reset_out, RstDone, StkDec,
       StkEn, StkInc, StkLd, StkRst, Sub, xor_1_out;
  wire [4:0] MAddrOut, multiplexer_1_out, PrAddr;
  wire [7:0] A_q7, ALU_p18, B_q7, counterpreset_1_out, driver_1_out, Inst_q7, multiplexer_2_out, PrData,
       stack_register_1_q;

  and and_1 (and_1_out, Rdy, RstDone);
  xor xor_1 (xor_1_out, and_2_out, RstDone);
  and and_2 (and_2_out, clk_2, PrMode);
  Counter #(.Bits(5)) counter_1 (.en(1'b1), .C(xor_1_out), .clr(and_1_out), .out(PrAddr), .ovf(Rdy));
  not not_1 (PrMode, Rdy);
  Button Reset (.out(Reset_out));
  LED READY (.in(Rdy));
  clock_with_enable clock_with_enable_1 (.ClkI(clk), .En(Rdy), .ClkO(clock_with_enable_1_clko));
  control_logic control_logic_1 (
    .Clk(not_3_out), .Inst(Inst_q7), .AEq(AEq), .AGreater(AGreater), .AZero(AZero), .Reset(Reset_out),
    .PCOut(PCOut), .PCEnable(PCEnable), .PCClear(PCClear), .PCLd(PCLd), .ALUOut(ALUOut), .LdOut(LdOut),
    .LdA(LdA), .EnA(EnA), .LdB(LdB), .EnB(EnB), .Sub(Sub), .LdInst(LdInst), .EnInst(EnInst),
    .LdMAddr(LdMAddr), .MWr(MWr), .MEn(MEn), .Hlt(Hlt), .LdFlags(LdFlags), .EnGnd(EnGnd), .RstDone(RstDone),
    .StkEn(StkEn), .StkLd(StkLd), .StkInc(StkInc), .StkDec(StkDec), .StkRst(StkRst));
  ROM #(.AddrBits(5), .isProgramMemory("true"), .Bits(8)) rom_1 (.A(PrAddr), .sel(1'b1), .D(PrData));
  not not_2 (not_2_out, Hlt);
  and and_3 (and_3_out, not_2_out, clock_with_enable_1_clko);
  or or_1 (or_1_out, MWr, PrMode);
  not not_3 (not_3_out, and_3_out);
  _8_bit_reg A (
    .Load(LdA), .Clk(and_3_out), .D7(driver_1_out[7]), .D6(driver_1_out[6]), .D5(driver_1_out[5]),
    .D4(driver_1_out[4]), .D3(driver_1_out[3]), .D2(driver_1_out[2]), .D1(driver_1_out[1]),
    .D0(driver_1_out[0]), .Q7(A_q7[7]), .Q6(A_q7[6]), .Q5(A_q7[5]), .Q4(A_q7[4]), .Q3(A_q7[3]), .Q2(A_q7[2]),
    .Q1(A_q7[1]), .Q0(A_q7[0]));
  _8_bit_reg B (
    .Load(LdB), .Clk(and_3_out), .D7(driver_1_out[7]), .D6(driver_1_out[6]), .D5(driver_1_out[5]),
    .D4(driver_1_out[4]), .D3(driver_1_out[3]), .D2(driver_1_out[2]), .D1(driver_1_out[1]),
    .D0(driver_1_out[0]), .Q7(B_q7[7]), .Q6(B_q7[6]), .Q5(B_q7[5]), .Q4(B_q7[4]), .Q3(B_q7[3]), .Q2(B_q7[2]),
    .Q1(B_q7[1]), .Q0(B_q7[0]));
  _8_bit_reg Inst (
    .Load(LdInst), .Clk(and_3_out), .D7(driver_1_out[7]), .D6(driver_1_out[6]), .D5(driver_1_out[5]),
    .D4(driver_1_out[4]), .D3(driver_1_out[3]), .D2(driver_1_out[2]), .D1(driver_1_out[1]),
    .D0(driver_1_out[0]), .Q7(Inst_q7[7]), .Q6(Inst_q7[6]), .Q5(Inst_q7[5]), .Q4(Inst_q7[4]),
    .Q3(Inst_q7[3]), .Q2(Inst_q7[2]), .Q1(Inst_q7[1]), .Q0(Inst_q7[0]));
  not not_4 (not_4_out, PrMode);
  and and_4 (and_4_out, not_4_out, MEn);
  assign driver_1_out = EnA ? A_q7 : 8'bz;  // Driver driver_1
  assign driver_1_out = EnB ? B_q7 : 8'bz;  // Driver driver_2
  assign driver_1_out = EnInst ? Inst_q7 : 8'bz;  // Driver driver_3
  or or_2 (or_2_out, and_3_out, and_2_out);
  assign driver_1_out = EnGnd ? {8{1'b0}} : 8'bz;  // Driver driver_4
  or or_3 (or_3_out, InspectMode, and_4_out);
  assign driver_1_out = ALUOut ? ALU_p18 : 8'bz;  // Driver driver_5
  assign driver_1_out = PCOut ? counterpreset_1_out : 8'bz;  // Driver driver_6
  Multiplexer #(.Selector_Bits(2), .Bits(5)) multiplexer_1 (
    .sel({InspectMode, PrMode}), .in_0(MAddrOut), .in_1(PrAddr), .in_2(InspectAddr), .in_3({5{1'b0}}),
    .out(multiplexer_1_out));
  // ALU ALU: pin names not known; wires that end beside it: Sub, A_q7[7], A_q7[6], A_q7[5], A_q7[4], A_q7[3], A_q7[2], A_q7[1], A_q7[0], B_q7[7], B_q7[6], B_q7[5], B_q7[4], B_q7[3], B_q7[2], B_q7[1], B_q7[0], ALU_p18[7], ALU_p18[6], ALU_p18[5], ALU_p18[4], ALU_p18[3], ALU_p18[2], ALU_p18[1], ALU_p18[0], ALU_p26, ALU_p27, ALU_p28
  _8_bit_reg _8_bit_reg_1 (
    .Load(LdOut), .Clk(and_3_out), .D7(driver_1_out[7]), .D6(driver_1_out[6]), .D5(driver_1_out[5]),
    .D4(driver_1_out[4]), .D3(driver_1_out[3]), .D2(driver_1_out[2]), .D1(driver_1_out[1]),
    .D0(driver_1_out[0]), .Q7(Hi3), .Q6(Hi2), .Q5(Hi1), .Q4(Hi0), .Q3(Lo3), .Q2(Lo2), .Q1(Lo1), .Q0(Lo0));
  CounterPreset #(.Bits(8)) counterpreset_1 (
    .en(PCEnable), .C(and_3_out), .dir(1'b0), .in(driver_1_out), .ld(PCLd), .clr(PCClear),
    .out(counterpreset_1_out));  // open: ovf
  Seven_Seg seven_seg_1 (.a(HiA), .b(HiB), .c(HiC), .d(HiD), .e(HiE), .f(HiF), .g(HiG), .dp(HiDP));
  _32_byte_ram _32_byte_ram_1 (
    .Bus(multiplexer_2_out), .Addr(multiplexer_1_out), .Wr(or_1_out), .Clk(or_2_out), .En(or_3_out),
    .Out(driver_1_out));
  _8_bit_reg Flags_Register (
    .Load(LdFlags), .Clk(and_3_out), .D7(1'b0), .D6(1'b0), .D5(1'b0), .D4(1'b0), .D3(1'b0), .D2(ALU_p26),
    .D1(ALU_p27), .D0(ALU_p28), .Q2(AEq), .Q1(AGreater), .Q0(AZero));  // open: Q7, Q6, Q5, Q4, Q3
  Seven_Seg seven_seg_2 (.a(LoA), .b(LoB), .c(LoC), .d(LoD), .e(LoE), .f(LoF), .g(LoG), .dp(LoDP));
  _8_bit_reg MAddr (
    .Load(LdMAddr), .Clk(and_3_out), .D7(driver_1_out[7]), .D6(driver_1_out[6]), .D5(driver_1_out[5]),
    .D4(driver_1_out[4]), .D3(driver_1_out[3]), .D2(driver_1_out[2]), .D1(driver_1_out[1]),
    .D0(driver_1_out[0]), .Q7(MAddr_q7), .Q6(MAddr_q6), .Q5(MAddr_q5), .Q4(MAddrOut[4]), .Q3(MAddrOut[3]),
    .Q2(MAddrOut[2]), .Q1(MAddrOut[1]), .Q0(MAddrOut[0]));
  Multiplexer #(.Bits(8)) multiplexer_2 (.sel(PrMode), .in_0(driver_1_out), .in_1(PrData), .out(multiplexer_2_out));
  hex_display_decoder HiDecoder (
    ._3(Hi3), ._2(Hi2), ._1(Hi1), ._0(Hi0), .A(HiA), .B(HiB), .C(HiC), .D(HiD), .E(HiE), .F(HiF), .G(HiG),
    .DP(HiDP));
  hex_display_decoder LoDecoder (
    ._3(Lo3), ._2(Lo2), ._1(Lo1), ._0(Lo0), .A(LoA), .B(LoB), .C(LoC), .D(LoD), .E(LoE), .F(LoF), .G(LoG),
    .DP(LoDP));
  stack_register stack_register_1 (
    .Ld(StkLd), .Clk(and_3_out), .Inc(StkInc), .Dec(StkDec), .Rst(StkRst), .D(driver_1_out),
    .Q(stack_register_1_q));
  assign driver_1_out = StkEn ? stack_register_1_q : 8'bz;  // Driver driver_7

  // Notes on the sheet:
  //   clk: Hz: 50
  //   clk_2: Hz: 50
  //   contents of rom_1 (hex, n*v repeats v):
  //   1,a,2,16,1e,1f,4*0,14
  //   Output Register and Hex Display Decoder
endmodule
