// Digital circuit control_logic.dig as structural Verilog
module control_logic (
  input  Clk,
  input  [7:0] Inst,
  output PCOut,
  output PCEnable,
  output PCClear,
  output PCLd,
  output ALUOut,
  output LdOut,
  output LdA,
  output EnA,
  output LdB,
  output EnB,
  output Sub,
  output LdInst,
  output EnInst,
  output LdMAddr,
  output MWr,
  output MEn,
  output Hlt
);

  wire [2:0] counter_1_out;
  wire [17:17] rom_1_d;

  Counter #(.Bits(3)) counter_1 (.en(1'b1), .C(Clk), .clr(rom_1_d[17]), .out(counter_1_out));  // open: ovf
  ROM #(.AddrBits(8), .isProgramMemory("true"), .Bits(18)) rom_1 (
    .A({Inst[4:0], counter_1_out}), .sel(1'b1),
    .D({rom_1_d[17], Hlt, MEn, MWr, LdMAddr, EnInst, LdInst, Sub, EnB, LdB, EnA, LdA, LdOut, ALUOut, PCLd, PCClear, PCEnable, PCOut}));

  // Notes on the sheet:
  //   // Ignore the 3 high bits, reserved for the microcode counter
  //   rom_1 loads rom.hex
endmodule
